# Fritzing sketch layout (saved by Fritzing 0.9.3b)

parts:
  Composant1 = Arduino Nano (Rev3.0)
  HM10 = Bluetooth HC-05 Macho
  LED_RING = 12 NeoPixel Ring [part_number=1643]

nets:
  GND: Composant1.GND, HM10.GND, LED_RING.GND
  N1: Composant1.D2, HM10.TXD
  N2: Composant1.D3, HM10.RXD
  N3: Composant1.D6, LED_RING.IN
  5V: Composant1.5V, HM10.VCC, LED_RING.VDD

custom parts:
  12 NeoPixel Ring: 12 ultra bright smart LED NeoPixels are arranged in a circle with 1.5" (37mm) outer diameter. The rings are 'chainable' - connect the output pin of one to the input pin of another. Use only one microcontroller pin to control as many as you can chain together! Each LED is addressable as the driver chip is inside the LED. Each one has ~18mA constant current drive so the color will be very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
